// Logisim project ALU Project207.circ as structural Verilog
module main (
  input  [3:0] in_1,
  input  [3:0] in_2,
  input  [3:0] in_3,
  output [3:0] out_4,
  output [3:0] out_5
);

  wire [3:0] and_1_out, and_2_out, xor_1_out;

  assign xor_1_out = in_1 ^ in_2;  // XOR_Gate xor_1, 4 bits wide
  assign and_1_out = in_2 & in_1;  // AND_Gate and_1, 4 bits wide
  assign and_2_out = xor_1_out & in_3;  // AND_Gate and_2, 4 bits wide
  assign out_4 = xor_1_out ^ in_3;  // XOR_Gate xor_2, 4 bits wide
  assign out_5 = and_2_out | and_1_out;  // OR_Gate or_1, 4 bits wide
endmodule

module ALU (
  input  A3,
  input  A2,
  input  A1,
  input  A0,
  input  B3,
  input  B2,
  input  B1,
  input  B0,
  input  in_9,
  input  S0,
  input  S1,
  input  S2,
  input  E_D,
  output out_14,
  output out_15,
  output out_16,
  output out_17,
  output out_18,
  output out_19,
  output out_20,
  output out_21
);

  wire adder_1_out_10, adder_1_out_11, adder_1_out_12, adder_1_out_13, and_2_out, and_3_out, and_4_out,
       and_5_out, not_1_out, not_2_out, not_3_out, not_4_out, or_1_out, or_2_out, or_3_out, or_4_out,
       xor_1_out, xor_2_out, xor_3_out, xor_4_out;

  // AND_Gate and_1 has open pins: in0=S0, in1=S1, in2=S2, out=open
  or or_1 (or_1_out, A0, B0);
  xor xor_1 (xor_1_out, A0, B0);
  Multiplexer #(.select(3)) multiplexer_1 (
    .in0(xor_1_out), .in1(or_1_out), .in2(not_1_out), .in3(adder_1_out_12), .in4(B0), .in5(adder_1_out_12),
    .in7(and_2_out), .out(out_14), .sel({S2, S1, S0}), .en(E_D));  // open: in6
  not not_1 (not_1_out, A0);
  and and_2 (and_2_out, A0, B0);
  xor xor_2 (xor_2_out, A1, B1);
  or or_2 (or_2_out, A1, B1);
  not not_2 (not_2_out, A1);
  Multiplexer #(.select(3)) multiplexer_2 (
    .in0(xor_2_out), .in1(or_2_out), .in2(not_2_out), .in3(adder_1_out_13), .in4(B1), .in5(adder_1_out_13),
    .in7(and_3_out), .out(out_15), .sel({S2, S1, S0}), .en(E_D));  // open: in6
  and and_3 (and_3_out, A1, B1);
  Adder adder_1 (
    .in_5(in_9), .in_8(A0), .in_6(A1), .in_7(A2), .in_9(A3), .in_1(B0), .in_2(B1), .in_3(B2), .in_4(B3),
    .out_12(adder_1_out_12), .out_13(adder_1_out_13), .out_11(adder_1_out_11), .out_10(adder_1_out_10));
  or or_3 (or_3_out, A2, B2);
  xor xor_3 (xor_3_out, A2, B2);
  Multiplexer #(.select(3)) multiplexer_3 (
    .in0(xor_3_out), .in1(or_3_out), .in2(not_3_out), .in3(adder_1_out_11), .in4(B2), .in5(adder_1_out_11),
    .in7(and_4_out), .out(out_16), .sel({S2, S1, S0}), .en(E_D));  // open: in6
  and and_4 (and_4_out, A2, B2);
  not not_3 (not_3_out, A2);
  xor xor_4 (xor_4_out, A3, B3);
  Multiplexer #(.select(3)) multiplexer_4 (
    .in0(xor_4_out), .in1(or_4_out), .in2(not_4_out), .in3(adder_1_out_10), .in4(B3), .in5(adder_1_out_10),
    .in7(and_5_out), .out(out_17), .sel({S2, S1, S0}), .en(E_D));  // open: in6
  not not_4 (not_4_out, A3);
  or or_4 (or_4_out, A3, B3);
  and and_5 (and_5_out, A3, B3);

  assign out_18 = out_17;
  assign out_19 = out_16;
  assign out_20 = out_15;
  assign out_21 = out_14;
endmodule

// Full Adder
module Adder (
  input  in_1,
  input  in_2,
  input  in_3,
  input  in_4,
  input  in_5,
  input  in_6,
  input  in_7,
  input  in_8,
  input  in_9,
  output out_10,
  output out_11,
  output out_12,
  output out_13
);

  wire [3:0] xor_4_out;

  xor xor_1 (xor_4_out[3], in_5, in_1);
  Adder_part #(.width(4)) adder_1 (
    .a(xor_4_out), .b({in_8, in_6, in_7, in_9}), .out({out_12, out_13, out_11, out_10}), .cin(in_5));  // open: cout
  xor xor_2 (xor_4_out[2], in_5, in_2);
  xor xor_3 (xor_4_out[1], in_5, in_3);
  xor xor_4 (xor_4_out[0], in_5, in_4);
endmodule
